// Digital circuit Lab00b.dig as structural Verilog
module Lab00b (
);

  wire switch1_b, switch2_b;

  Switch #(.switchActsAsInput("true")) switch2 (.A(1'b1), .B(switch2_b));
  Switch #(.switchActsAsInput("true")) switch1 (.A(switch2_b), .B(switch1_b));
  // PolarityAwareLED led1: pin names not known; wires that end beside it: switch1_b, 1'b0
endmodule
